# Fritzing sketch rp2040 and ADS1015 (saved by Fritzing 0.9.3b)

parts:
  Pico1 = Raspberry Pi Pico
  Part1 = Adafruit ADS1015 12Bit I2C ADC [part_number="Adafruit #1083"]

nets:
  GND: Pico1.GND, Part1.GND
  3V3: Pico1.3V3, Part1.VDD
  N1: Pico1.GP1, Part1.SCL
  N2: Pico1.GP0, Part1.SDA

custom parts:
  Raspberry Pi Pico: Raspberry Pi Pico. Based around the RP2040 microcontroller the Pico is a low cost microcontroller device bringing Raspberry Pi quality, cost, and easy of use to the microcontroller space.
  Adafruit ADS1015 12Bit I2C ADC: For microcontrollers without an analog-to-digital converter or when you want a higher-precision ADC, the ADS1015 provides 12-bit precision at 3300 samples/second over I2C. The chip can be configured as 4 single-ended input channels, or two differential channels. As a nice bonus, it even includes a programmable gain amplifier, up to x16, to help boost up smaller single/differential signals to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
