# Fritzing sketch rp2040 and HTU31D (saved by Fritzing 0.9.3b)

parts:
  Pico1 = Raspberry Pi Pico
  Part2 = HTU21D-F Temperature + Humidity Sensor

nets:
  GND: Pico1.GND, Part2.GND
  3V3: Pico1.3V3, Part2.+3V3
  N1: Pico1.GP1, Part2.SCL
  N2: Pico1.GP0, Part2.SDA

custom parts:
  Raspberry Pi Pico: Raspberry Pi Pico. Based around the RP2040 microcontroller the Pico is a low cost microcontroller device bringing Raspberry Pi quality, cost, and easy of use to the microcontroller space.
  HTU21D-F Temperature + Humidity Sensor: This I2C digital humidity sensor is an accurate and intelligent alternative to the much simpler Humidity and Temperature Sensor - SHT15 Breakout It has a typical accuracy of ±2% with an operating range that's optimized from 5% to 95% RH. Operation outside this range is still possible - just the accuracy might drop a bit. The temperature output has an accuracy of ±1°C from -30~90°C. If you're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
