# Fritzing sketch rp2040 and TSL2591 (saved by Fritzing 0.9.3b)

parts:
  Pico1 = Raspberry Pi Pico
  Part6 = Adafruit TSL2591 [part_number="Adafruit #1980"]

nets:
  GND: Pico1.GND, Part6.GND
  3V3: Pico1.3V3, Part6.VIN
  N1: Pico1.GP1, Part6.SCL
  N2: Pico1.GP0, Part6.SDA

custom parts:
  Raspberry Pi Pico: Raspberry Pi Pico. Based around the RP2040 microcontroller the Pico is a low cost microcontroller device bringing Raspberry Pi quality, cost, and easy of use to the microcontroller space.
  Adafruit TSL2591: When the future is dazzlingly-bright, this ultra-high-range luminosity sensor will help you measure it. The TSL2591 luminosity sensor is an advanced digital light sensor, ideal for use in a wide range of light situations. Compared to low cost CdS cells, this sensor is more precise, allowing for exact lux calculations and can be configured for different gain/timing ranges to detect light ranges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
