# Fritzing sketch rp2040 and VCNL4010 (saved by Fritzing 0.9.3b)

parts:
  Pico1 = Raspberry Pi Pico
  Part5 = Adafruit VCNL4010 Proximity and Light sensor [part_number="Adafruit #466"]

nets:
  GND: Pico1.GND, Part5.GND
  3V3: Pico1.3V3, Part5.VIN
  N1: Pico1.GP1, Part5.SCL
  N2: Pico1.GP0, Part5.SDA

custom parts:
  Raspberry Pi Pico: Raspberry Pi Pico. Based around the RP2040 microcontroller the Pico is a low cost microcontroller device bringing Raspberry Pi quality, cost, and easy of use to the microcontroller space.
  Adafruit VCNL4010 Proximity and Light sensor: The VCNL4010 sensor is a nice way to add a small-distance proximity sensor to your microcontroller project. For longer distances (in the range of cm, you can use a SHARP IR distance sensor, but those are only good if the object is over 10 cm away. The VCNL4010 is designed for much shorter distances, no more than 200mm (about 7.5") and under our experimentation we found it worked best at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
