# Fritzing sketch rp2040 and VEML6075 (saved by Fritzing 0.9.3b)

parts:
  Pico1 = Raspberry Pi Pico
  Part2 = Adafruit VEML6075 UV Sensor Breakout [part_number=3964]

nets:
  GND: Pico1.GND, Part2.GND
  3V3: Pico1.3V3, Part2.3.3V
  N1: Pico1.GP1, Part2.SCL
  N2: Pico1.GP0, Part2.SDA

custom parts:
  Raspberry Pi Pico: Raspberry Pi Pico. Based around the RP2040 microcontroller the Pico is a low cost microcontroller device bringing Raspberry Pi quality, cost, and easy of use to the microcontroller space.
  Adafruit VEML6075 UV Sensor Breakout: This little sensor is a great way to add UVA and UVB light sensing to any microcontroller project. The VEML6075 from Vishay has both true UVA and UVB band light sensors and an I2C-controlled ADC that will take readings and integrate them. The sensor also comes with calibration registers so you can easily convert the UVA/UVB readings into the UV Index. Compared to our other UV sensors, this one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
