# Fritzing sketch rp2040 and dps310 (saved by Fritzing 0.9.3b)

parts:
  Pico1 = Raspberry Pi Pico
  Part6 = Adafruit DPS310 Precision Barometric Pressure and Altitude Sensor [part_number="Adafruit #4494"]

nets:
  GND: Pico1.GND, Part6.GND
  3V3: Pico1.3V3, Part6.VCC
  N1: Pico1.GP1, Part6.SCK/SCL
  N2: Pico1.GP0, Part6.SDI/SDA

custom parts:
  Raspberry Pi Pico: Raspberry Pi Pico. Based around the RP2040 microcontroller the Pico is a low cost microcontroller device bringing Raspberry Pi quality, cost, and easy of use to the microcontroller space.
  Adafruit DPS310 Precision Barometric Pressure and Altitude Sensor: How high are you right now? If you had a precision altitude sensor, you would know for sure! The DPS310 sensor from Infineon a high precision barometric sensor, perfect for measuring altitude changes with a up to ±0.002 hPa (or ±0.02 m) precision high precision mode and ± 1 hPa absolute accuracy. That means you can know your absolute altitude with 1 meter accuracy when you set the sea-level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
