# Fritzing sketch rp2040 and sht40 (saved by Fritzing 0.9.3b)

parts:
  Pico1 = Raspberry Pi Pico
  Part4 = Adafruit SHT40

nets:
  GND: Pico1.GND, Part4.GND
  3V3: Pico1.3V3, Part4.VCC
  N1: Pico1.GP1, Part4.SCL
  N2: Pico1.GP0, Part4.SDA

custom parts:
  Raspberry Pi Pico: Raspberry Pi Pico. Based around the RP2040 microcontroller the Pico is a low cost microcontroller device bringing Raspberry Pi quality, cost, and easy of use to the microcontroller space.
  Adafruit SHT40: Sensirion Temperature/Humidity sensors are some of the finest & highest-accuracy devices you can get. And finally, we have some that have a true I2C interface for easy reading. The SHT40 sensor is the fourth generation (started at the SHT10 and worked its way up to the top!). The SHT40 has an excellent ±1.8% typical relative humidity accuracy from 25 to 75% and ±0.2 °C typical accuracy from 0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
