# Fritzing sketch rp2040 and tcs34725 (saved by Fritzing 0.9.3b)

parts:
  Pico1 = Raspberry Pi Pico
  Part3 = Adafruit TCS34725 RGB Color Sensor [part_number="Adafruit #1334"]

nets:
  GND: Pico1.GND, Part3.GND
  3V3: Pico1.3V3, Part3.+3V3
  N1: Pico1.GP1, Part3.SCL
  N2: Pico1.GP0, Part3.SDA

custom parts:
  Raspberry Pi Pico: Raspberry Pi Pico. Based around the RP2040 microcontroller the Pico is a low cost microcontroller device bringing Raspberry Pi quality, cost, and easy of use to the microcontroller space.
  Adafruit TCS34725 RGB Color Sensor: Your electronics can now see in dazzling color with this lovely color light sensor. We found the best color sensor on the market, the TCS34725, which has RGB and Clear light sensing elements. An IR blocking filter, integrated on-chip and localized to the color sensing photodiodes, minimizes the IR spectral component of the incoming light and allows color measurements to be made accurately. The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
