# Fritzing sketch rp2040 and tlv490d (saved by Fritzing 0.9.3b)

parts:
  Pico1 = Raspberry Pi Pico
  Part1 = Adafruit TLV493D

nets:
  GND: Pico1.GND, Part1.GND
  3V3: Pico1.3V3, Part1.VCC
  N1: Pico1.GP1, Part1.SCL
  N2: Pico1.GP0, Part1.SDA

custom parts:
  Raspberry Pi Pico: Raspberry Pi Pico. Based around the RP2040 microcontroller the Pico is a low cost microcontroller device bringing Raspberry Pi quality, cost, and easy of use to the microcontroller space.
  Adafruit TLV493D: The TLV493D 3-axis magnetometer is a great little sensor for detecting magnets in 3D. The manufacturer Infineon suggests it could be used to make a joystick! You could also use it for other cool things like detecting objects with magnets attached, like the lid of a box, or maybe a statue that unlocks your secret lair when placed on your mantle! The TLD493D excels at measuring nearby magnetic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
