# Fritzing sketch rp2040 and vcnl4040 (saved by Fritzing 0.9.3b)

parts:
  Pico1 = Raspberry Pi Pico
  Adafruit_VCNL1 = Adafruit VCNL4040

nets:
  GND: Pico1.GND, Adafruit_VCNL1.GND
  3V3: Pico1.3V3, Adafruit_VCNL1.3.3V
  N1: Pico1.GP1, Adafruit_VCNL1.SCL
  N2: Pico1.GP0, Adafruit_VCNL1.SDA

custom parts:
  Raspberry Pi Pico: Raspberry Pi Pico. Based around the RP2040 microcontroller the Pico is a low cost microcontroller device bringing Raspberry Pi quality, cost, and easy of use to the microcontroller space.
