# Fritzing sketch rp2040 and veml7700 (saved by Fritzing 0.9.3b)

parts:
  Pico1 = Raspberry Pi Pico
  Part4 = VEML7700 [part_number="Adafruit #4162"]

nets:
  GND: Pico1.GND, Part4.GND
  3V3: Pico1.3V3, Part4.VIN
  N1: Pico1.GP1, Part4.SCL
  N2: Pico1.GP0, Part4.SDA

custom parts:
  Raspberry Pi Pico: Raspberry Pi Pico. Based around the RP2040 microcontroller the Pico is a low cost microcontroller device bringing Raspberry Pi quality, cost, and easy of use to the microcontroller space.
