# Fritzing sketch rp2040 and vl6180x (saved by Fritzing 0.9.3b)

parts:
  Pico1 = Raspberry Pi Pico
  Part3 = Adafruit VL6180X Time of Flight Distance Sensor [part_number="Adafruit #3316"]

nets:
  GND: Pico1.GND, Part3.GND
  3V3: Pico1.3V3, Part3.VIN
  N1: Pico1.GP1, Part3.SCL
  N2: Pico1.GP0, Part3.SDA

custom parts:
  Raspberry Pi Pico: Raspberry Pi Pico. Based around the RP2040 microcontroller the Pico is a low cost microcontroller device bringing Raspberry Pi quality, cost, and easy of use to the microcontroller space.
  Adafruit VL6180X Time of Flight Distance Sensor: The VL6180X is a Time of Flight distance sensor like no other you've used! The sensor contains a very tiny invisible laser source, and a matching sensor. The VL6180X can detect the "time of flight", or how long the light has taken to bounce back to the sensor. Since it uses a very narrow light source, it is good for determining distance of only the surface directly in front of it. Unlike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
